// Logisim project 74ls181.circ as structural Verilog: 2 circuits, main circuit sn74ls181
module sn74ls181 (
  input  s0,
  input  s1,
  input  s2,
  input  s3,
  input  B3,
  input  A3,
  input  B2,
  input  A2,
  input  B1,
  input  A1,
  input  B0,
  input  A0,
  input  M,
  input  Cin,
  output notG_or_Y,
  output Cout,
  output notP_or_X,
  output F3,
  output F2,
  output A_eq_B,
  output F1,
  output F0
);

  wire and_1_out, and_1bit_1_out_2, and_1bit_2_out_2, and_1bit_3_out_2, and_1bit_4_out_2, and_1bit_5_out_2,
       and_2_out, and_3_out, and_4_out, and_5_out, and_6_out, and_7_out, and_8_out, and_9_out, and_10_out,
       and_11_out, and_12_out, and_13_out, and_14_out, and_15_out, and_16_out, and_17_out, and_18_out,
       and_19_out, and_20_out, and_21_out, and_22_out, and_23_out, and_24_out, and_25_out, and_26_out,
       and_27_out, and_28_out, nand_1_out, nand_3_out, nor_1_out, nor_2_out, nor_3_out, nor_4_out, nor_5_out,
       nor_6_out, nor_7_out, nor_8_out, nor_10_out, nor_11_out, nor_12_out, not_1_out, not_2_out, not_3_out,
       not_4_out, not_5_out, not_6_out, not_7_out, xor_1_out, xor_2_out, xor_3_out, xor_4_out;

  not not_1 (not_1_out, B3);
  not not_2 (not_2_out, B2);
  not not_3 (not_3_out, B1);
  not not_4 (not_4_out, B0);
  not not_5 (not_5_out, M);
  and and_1 (and_1_out, B3, s3, A3);
  and and_2 (and_2_out, A3, s2, not_1_out);
  and and_3 (and_3_out, not_1_out, s1);
  and and_4 (and_4_out, s0, B3);
  and_1bit and_1bit_1 (.in_1(A3), .out_2(and_1bit_1_out_2));
  and and_5 (and_5_out, B2, s3, A2);
  nor nor_1 (nor_1_out, and_5_out, and_6_out);
  and and_6 (and_6_out, A2, s2, not_2_out);
  and and_7 (and_7_out, not_2_out, s1);
  and and_8 (and_8_out, s0, B2);
  and_1bit and_1bit_2 (.in_1(A2), .out_2(and_1bit_2_out_2));
  and and_9 (and_9_out, B1, s3, A1);
  nor nor_2 (nor_2_out, and_9_out, and_10_out);
  and and_10 (and_10_out, A1, s2, not_3_out);
  and and_11 (and_11_out, not_3_out, s1);
  and and_12 (and_12_out, s0, B1);
  and_1bit and_1bit_3 (.in_1(A1), .out_2(and_1bit_3_out_2));
  and and_13 (and_13_out, B0, s3, A0);
  and and_14 (and_14_out, A0, s2, not_4_out);
  and and_15 (and_15_out, not_4_out, s1);
  and and_16 (and_16_out, s0, B0);
  and_1bit and_1bit_4 (.in_1(A0), .out_2(and_1bit_4_out_2));
  nor nor_3 (nor_3_out, and_1_out, and_2_out);
  nor nor_4 (nor_4_out, and_3_out, and_4_out, and_1bit_1_out_2);
  nor nor_5 (nor_5_out, and_7_out, and_8_out, and_1bit_2_out_2);
  nor nor_6 (nor_6_out, and_11_out, and_12_out, and_1bit_3_out_2);
  nor nor_7 (nor_7_out, and_13_out, and_14_out);
  nor nor_8 (nor_8_out, and_15_out, and_16_out, and_1bit_4_out_2);
  xor xor_1 (xor_1_out, nor_3_out, nor_4_out);
  xor xor_2 (xor_2_out, nor_1_out, nor_5_out);
  xor xor_3 (xor_3_out, nor_2_out, nor_6_out);
  xor xor_4 (xor_4_out, nor_7_out, nor_8_out);
  and_1bit and_1bit_5 (.in_1(nor_4_out), .out_2(and_1bit_5_out_2));
  and and_17 (and_17_out, nor_3_out, nor_5_out);
  and and_18 (and_18_out, nor_3_out, nor_1_out, nor_6_out);
  and and_19 (and_19_out, nor_3_out, nor_1_out, nor_2_out, nor_8_out);
  nand nand_1 (nand_1_out, nor_3_out, nor_1_out, nor_2_out, nor_7_out, Cin);
  nand nand_2 (notP_or_X, nor_3_out, nor_1_out, nor_2_out, nor_7_out);
  and and_20 (and_20_out, Cin, nor_7_out, nor_2_out, nor_1_out, not_5_out);
  and and_21 (and_21_out, nor_2_out, nor_1_out, nor_8_out, not_5_out);
  and and_22 (and_22_out, nor_1_out, nor_6_out, not_5_out);
  and and_23 (and_23_out, nor_5_out, not_5_out);
  and and_24 (and_24_out, Cin, nor_7_out, nor_2_out, not_5_out);
  and and_25 (and_25_out, nor_2_out, nor_8_out, not_5_out);
  and and_26 (and_26_out, nor_6_out, not_5_out);
  and and_27 (and_27_out, Cin, nor_7_out, not_5_out);
  and and_28 (and_28_out, nor_8_out, not_5_out);
  nand nand_3 (nand_3_out, Cin, not_5_out);
  nor nor_9 (notG_or_Y, and_1bit_5_out_2, and_17_out, and_18_out, and_19_out);
  not not_6 (not_6_out, notG_or_Y);
  not not_7 (not_7_out, nand_1_out);
  nor nor_10 (nor_10_out, and_20_out, and_21_out, and_22_out, and_23_out);
  nor nor_11 (nor_11_out, and_24_out, and_25_out, and_26_out);
  nor nor_12 (nor_12_out, and_27_out, and_28_out);
  or or_1 (Cout, not_6_out, not_7_out);
  xor xor_5 (F3, xor_1_out, nor_10_out);
  xor xor_6 (F2, xor_2_out, nor_11_out);
  xor xor_7 (F1, xor_3_out, nor_12_out);
  xor xor_8 (F0, xor_4_out, nand_3_out);
  and and_29 (A_eq_B, F3, F2, F1, F0);
endmodule

module and_1bit (
  input  in_1,
  output out_2
);

  and and_1 (out_2, in_1, in_1);
endmodule
