// Logisim project control_logic.circ as structural Verilog: 5 circuits, main circuit control_unit
module AluOp_unit (
  input  a,
  input  b,
  input  c,
  input  d,
  input  e,
  input  isLUI,
  input  isJumping,
  output AluSrc2,
  output [3:0] AluOp,
  output M,
  output Cn
);

  wire and_1_out, comparator_1_eq, comparator_2_eq, multiplexer_1_out, multiplexer_2_out, multiplexer_3_out,
       multiplexer_4_out, not_1_out, not_2_out, not_3_out, not_4_out, not_5_out, not_6_out, not_7_out,
       not_8_out, not_9_out, or_1_out, or_2_out, xor_1_out, xor_2_out, xor_3_out;

  not not_1 (not_1_out, e);
  Comparator #(.width(3)) comparator_1 (.a(3'b011), .b({c, d, e}), .eq(comparator_1_eq));  // open: gt, lt
  Comparator #(.width(2)) comparator_2 (.a({d, e}), .b(2'b01), .eq(comparator_2_eq));  // open: gt, lt
  and and_1 (and_1_out, c, comparator_2_eq);
  Multiplexer multiplexer_1 (.in0(e), .in1(not_1_out), .out(multiplexer_1_out), .sel(and_1_out));
  or or_1 (or_1_out, comparator_1_eq, comparator_2_eq);
  not not_2 (not_2_out, d);
  xor xor_1 (xor_1_out, c, e);
  xor xor_2 (xor_2_out, e, d);
  not not_3 (not_3_out, xor_2_out);
  Multiplexer multiplexer_2 (.in0(xor_2_out), .in1(not_3_out), .out(multiplexer_2_out), .sel(comparator_1_eq));
  Multiplexer multiplexer_3 (.in0(or_1_out), .in1(not_4_out), .out(multiplexer_3_out), .sel(multiplexer_2_out));
  not not_4 (not_4_out, or_1_out);
  Multiplexer multiplexer_4 (.in0(d), .in1(not_2_out), .out(multiplexer_4_out), .sel(not_5_out));
  not not_5 (not_5_out, or_2_out);
  or or_2 (or_2_out, xor_1_out, not_6_out);
  not not_6 (not_6_out, e);
  not not_7 (not_7_out, d);
  or or_3 (AluOp[3], isLUI, or_1_out);
  or or_4 (AluOp[2], multiplexer_3_out, isJumping);
  or or_5 (AluOp[1], isLUI, multiplexer_4_out);
  or or_6 (AluOp[0], multiplexer_1_out, isJumping);
  xor xor_3 (xor_3_out, c, e);
  not not_8 (not_8_out, xor_3_out);
  not not_9 (not_9_out, d);
  or or_7 (Cn, not_7_out, e);
  and and_2 (M, not_8_out, not_9_out);

  assign AluSrc2 = b;

  // Notes on the sheet:
  //   011
  //   01
  //   c
  //   e
  //   c
  //   e
  //   d
  //   e
  //   d
  //   e
  //   0 -> register 1 -> immediate
  //   0000 -> not
  //   1001 -> add
  //   0110 -> sub
  //   0001 -> or
  //   1011 -> and
endmodule

module sn74ls181_tmp (
  input  s0,
  input  s1,
  input  s2,
  input  s3,
  input  B3,
  input  A3,
  input  B2,
  input  A2,
  input  B1,
  input  A1,
  input  B0,
  input  A0,
  input  M,
  input  Cin,
  output notG_or_Y,
  output Cout,
  output notP_or_X,
  output F3,
  output F2,
  output A_eq_B,
  output F1,
  output F0
);

  wire and_1_out, and_1bit_tmp_1_out_2, and_1bit_tmp_2_out_2, and_1bit_tmp_3_out_2, and_1bit_tmp_4_out_2,
       and_1bit_tmp_5_out_2, and_2_out, and_3_out, and_4_out, and_5_out, and_6_out, and_7_out, and_8_out,
       and_9_out, and_10_out, and_11_out, and_12_out, and_13_out, and_14_out, and_15_out, and_16_out,
       and_18_out, and_19_out, and_20_out, and_21_out, and_22_out, and_23_out, and_24_out, and_25_out,
       and_26_out, and_27_out, and_28_out, and_29_out, nand_1_out, nand_3_out, nor_1_out, nor_2_out,
       nor_3_out, nor_4_out, nor_5_out, nor_6_out, nor_7_out, nor_8_out, nor_10_out, nor_11_out, nor_12_out,
       not_1_out, not_2_out, not_3_out, not_4_out, not_5_out, not_6_out, not_7_out, xor_1_out, xor_2_out,
       xor_3_out, xor_4_out;

  not not_1 (not_1_out, B3);
  not not_2 (not_2_out, B2);
  not not_3 (not_3_out, B1);
  not not_4 (not_4_out, B0);
  not not_5 (not_5_out, M);
  and and_1 (and_1_out, B3, s3, A3);
  and and_2 (and_2_out, A3, s2, not_1_out);
  and and_3 (and_3_out, not_1_out, s1);
  and and_4 (and_4_out, s0, B3);
  and_1bit_tmp and_1bit_tmp_1 (.in_1(A3), .out_2(and_1bit_tmp_1_out_2));
  and and_5 (and_5_out, B2, s3, A2);
  nor nor_1 (nor_1_out, and_5_out, and_6_out);
  and and_6 (and_6_out, A2, s2, not_2_out);
  and and_7 (and_7_out, not_2_out, s1);
  and and_8 (and_8_out, s0, B2);
  and_1bit_tmp and_1bit_tmp_2 (.in_1(A2), .out_2(and_1bit_tmp_2_out_2));
  and and_9 (and_9_out, B1, s3, A1);
  nor nor_2 (nor_2_out, and_9_out, and_10_out);
  and and_10 (and_10_out, A1, s2, not_3_out);
  and and_11 (and_11_out, not_3_out, s1);
  and and_12 (and_12_out, s0, B1);
  and_1bit_tmp and_1bit_tmp_3 (.in_1(A1), .out_2(and_1bit_tmp_3_out_2));
  and and_13 (and_13_out, B0, s3, A0);
  and and_14 (and_14_out, A0, s2, not_4_out);
  and and_15 (and_15_out, not_4_out, s1);
  and and_16 (and_16_out, s0, B0);
  and_1bit_tmp and_1bit_tmp_4 (.in_1(A0), .out_2(and_1bit_tmp_4_out_2));
  // AND_Gate and_17 is placed but not wired
  nor nor_3 (nor_3_out, and_1_out, and_2_out);
  nor nor_4 (nor_4_out, and_3_out, and_4_out, and_1bit_tmp_1_out_2);
  nor nor_5 (nor_5_out, and_7_out, and_8_out, and_1bit_tmp_2_out_2);
  nor nor_6 (nor_6_out, and_11_out, and_12_out, and_1bit_tmp_3_out_2);
  nor nor_7 (nor_7_out, and_13_out, and_14_out);
  nor nor_8 (nor_8_out, and_15_out, and_16_out, and_1bit_tmp_4_out_2);
  // OR_Gate or_1 is placed but not wired
  xor xor_1 (xor_1_out, nor_3_out, nor_4_out);
  // OR_Gate or_2 is placed but not wired
  xor xor_2 (xor_2_out, nor_1_out, nor_5_out);
  xor xor_3 (xor_3_out, nor_2_out, nor_6_out);
  xor xor_4 (xor_4_out, nor_7_out, nor_8_out);
  and_1bit_tmp and_1bit_tmp_5 (.in_1(nor_4_out), .out_2(and_1bit_tmp_5_out_2));
  and and_18 (and_18_out, nor_3_out, nor_5_out);
  and and_19 (and_19_out, nor_3_out, nor_1_out, nor_6_out);
  and and_20 (and_20_out, nor_3_out, nor_1_out, nor_2_out, nor_8_out);
  nand nand_1 (nand_1_out, nor_3_out, nor_1_out, nor_2_out, nor_7_out, Cin);
  nand nand_2 (notP_or_X, nor_3_out, nor_1_out, nor_2_out, nor_7_out);
  and and_21 (and_21_out, Cin, nor_7_out, nor_2_out, nor_1_out, not_5_out);
  and and_22 (and_22_out, nor_2_out, nor_1_out, nor_8_out, not_5_out);
  and and_23 (and_23_out, nor_1_out, nor_6_out, not_5_out);
  and and_24 (and_24_out, nor_5_out, not_5_out);
  and and_25 (and_25_out, Cin, nor_7_out, nor_2_out, not_5_out);
  and and_26 (and_26_out, nor_2_out, nor_8_out, not_5_out);
  and and_27 (and_27_out, nor_6_out, not_5_out);
  and and_28 (and_28_out, Cin, nor_7_out, not_5_out);
  and and_29 (and_29_out, nor_8_out, not_5_out);
  nand nand_3 (nand_3_out, Cin, not_5_out);
  nor nor_9 (notG_or_Y, and_1bit_tmp_5_out_2, and_18_out, and_19_out, and_20_out);
  not not_6 (not_6_out, notG_or_Y);
  not not_7 (not_7_out, nand_1_out);
  nor nor_10 (nor_10_out, and_21_out, and_22_out, and_23_out, and_24_out);
  nor nor_11 (nor_11_out, and_25_out, and_26_out, and_27_out);
  nor nor_12 (nor_12_out, and_28_out, and_29_out);
  or or_3 (Cout, not_6_out, not_7_out);
  xor xor_5 (F3, xor_1_out, nor_10_out);
  xor xor_6 (F2, xor_2_out, nor_11_out);
  xor xor_7 (F1, xor_3_out, nor_12_out);
  xor xor_8 (F0, xor_4_out, nand_3_out);
  and and_30 (A_eq_B, F3, F2, F1, F0);
endmodule

module and_1bit_tmp (
  input  in_1,
  output out_2
);

  and and_1 (out_2, in_1, in_1);
endmodule

module control_unit_test (
  input  [4:0] Opcode,
  input  [3:0] A,
  input  [3:0] B,
  output Cout,
  output A_eq_B,
  output [3:0] ALU_out
);

  wire aluop_unit_1_cn, aluop_unit_1_m;
  wire [3:0] aluop_unit_1_aluop;

  AluOp_unit aluop_unit_1 (
    .a(Opcode[4]), .b(Opcode[3]), .c(Opcode[2]), .d(Opcode[1]), .e(Opcode[0]), .AluOp(aluop_unit_1_aluop),
    .M(aluop_unit_1_m), .Cn(aluop_unit_1_cn));  // open: isLUI, isJumping, AluSrc2
  sn74ls181_tmp sn74ls181_tmp_1 (
    .A1(A[1]), .B3(B[3]), .A3(A[3]), .B2(B[2]), .A2(A[2]), .B1(B[1]), .B0(B[0]), .A0(A[0]),
    .M(aluop_unit_1_m), .Cin(aluop_unit_1_cn), .s0(aluop_unit_1_aluop[0]), .s1(aluop_unit_1_aluop[1]),
    .s2(aluop_unit_1_aluop[2]), .s3(aluop_unit_1_aluop[3]), .F1(ALU_out[1]), .F0(ALU_out[0]), .Cout(Cout),
    .F3(ALU_out[3]), .F2(ALU_out[2]), .A_eq_B(A_eq_B));  // open: notG_or_Y, notP_or_X
endmodule

module control_unit (
  input  [4:0] Opcode,
  output [5:0] ALUOpExt,
  output isLUI,
  output RegWrite,
  output AluSrc2,
  output FlagWrite,
  output JumpSrc,
  output Jump,
  output Branch,
  output WriteRA,
  output AluSrc1,
  output ImmType0,
  output ImmType1,
  output isShift,
  output shiftType,
  output MemWrite,
  output MemRead,
  output MemToReg
);

  wire and_1_out, and_2_out, and_4_out, and_5_out, and_7_out, and_9_out, and_11_out, nand_1_out, nand_2_out,
       nor_1_out, not_1_out, not_2_out, not_3_out, not_4_out, not_5_out, not_6_out, not_7_out, not_8_out,
       not_9_out, not_10_out, not_11_out, not_12_out, not_13_out, not_14_out, not_15_out, xor_1_out,
       xor_2_out;

  nor nor_1 (nor_1_out, Opcode[0], Opcode[2]);
  and and_1 (and_1_out, Opcode[3], Opcode[4]);
  and and_2 (and_2_out, Opcode[4], Opcode[2]);
  and and_3 (isLUI, nor_1_out, and_1_out);
  xor xor_1 (xor_1_out, Opcode[0], Opcode[3]);
  not not_1 (not_1_out, Opcode[4]);
  not not_2 (not_2_out, Opcode[1]);
  and and_4 (and_4_out, not_1_out, Opcode[3], Opcode[2], not_2_out);
  not not_3 (not_3_out, Opcode[1]);
  not not_4 (not_4_out, Opcode[2]);
  not not_5 (not_5_out, Opcode[0]);
  not not_6 (not_6_out, Opcode[3]);
  not not_7 (not_7_out, Opcode[2]);
  AluOp_unit aluop_unit_1 (
    .a(Opcode[4]), .b(Opcode[3]), .c(Opcode[2]), .d(Opcode[1]), .e(Opcode[0]), .isLUI(isLUI),
    .AluOp(ALUOpExt[3:0]), .M(ALUOpExt[4]), .Cn(ALUOpExt[5]));  // open: isJumping, AluSrc2
  and and_5 (and_5_out, Opcode[4], xor_1_out);
  not not_8 (not_8_out, and_5_out);
  xor xor_2 (xor_2_out, Opcode[0], Opcode[1]);
  not not_9 (not_9_out, Opcode[2]);
  not not_10 (not_10_out, Opcode[4]);
  nand nand_1 (nand_1_out, Opcode[3], Opcode[1]);
  and and_6 (JumpSrc, Opcode[4], Opcode[0]);
  and and_7 (and_7_out, and_4_out, Opcode[0]);
  not not_11 (not_11_out, Opcode[4]);
  nand nand_2 (nand_2_out, Opcode[2], not_3_out, Opcode[0]);
  and and_8 (isShift, Opcode[3], not_4_out, not_5_out);
  not not_12 (not_12_out, Opcode[3]);
  not not_13 (not_13_out, Opcode[2]);
  and and_9 (and_9_out, Opcode[4], not_6_out, not_7_out, Opcode[1]);
  not not_14 (not_14_out, Opcode[0]);
  or or_1 (RegWrite, isLUI, not_8_out);
  not not_15 (not_15_out, Opcode[1]);
  xor xor_3 (AluSrc1, and_2_out, and_7_out);
  and and_10 (ImmType1, not_11_out, nand_2_out);
  and and_11 (and_11_out, Opcode[4], not_12_out, not_13_out, Opcode[1]);
  and and_12 (MemRead, and_9_out, not_14_out);
  and and_13 (FlagWrite, xor_2_out, not_9_out, not_10_out, nand_1_out);
  and and_14 (Jump, not_15_out, AluSrc1);
  and and_15 (ImmType0, AluSrc1, Opcode[1]);
  and and_16 (MemWrite, and_11_out, Opcode[0]);

  assign AluSrc2 = Opcode[3];
  assign Branch = AluSrc1;
  assign MemToReg = MemRead;
  assign shiftType = Opcode[1];
  assign WriteRA = AluSrc1;

  // Notes on the sheet:
  //   e
  //   d
  //   c
  //   b
  //   a
  //   a
  //   c
  //   e
  //   b
  //   not a
  //   b
  //   c
  //   not d
  //   a
  //   d
  //   a
  //   e
  //   d
  //   a
  //   e
  //   e
  //   c
  //   not d
  //   e
  //   b
  //   not c
  //   not e
  //   a
  //   d
  //   not b
  //   not c
  //   not c
  //   not a
  //   not b
  //   not c
  //   not e
  //   not d
  //   Branch
  //   not a
  //   e
  //   b
  //   d
  //   Contains ALUOp in [0-3] bits, Mode in [4] bit 
  //   and Cin in [5] bit
  //   1 if it's LUI operation else 0
  //   RegWrite = not(a and (b xor e)) or isLUI
  //   AluSrc2 = b
  //   FlagWrite = (e xor d) and not c and not a
  //   JumpSrc = 1 if the offset is in a register, 0 if it's immediate
  //   Jump = branch and not d
  //   Branch = PcSrc = WriteRA = AluSrc1 = (a and b) xor ( not a and b and c and not d and e)
  //   MemWrite = a and not b and not c and d and e
  //   It's active always except for "j", "jr", "b", "store" and "out"
  //   The second or operand is used to activate RegWrite also with "lui" instruction 
  //   Active only for "add", "addi" and "sub" instructions
  //   Jump = 1 if it's a jump instruction but not a branch
  //   First xor input is for "jalr", "j", "jr" and "b" instrctions
  //   Second xor input is for "jal" instruction
  //   ImmType0 = branch and d
  //   ImmType0 = 1 only with "b" instruction
  //   ImmType1 = not a and (not(c and not d and not e))
  //   ImmType1 = 1 only with logical-arithmetical instructions
  //   Nand used for excluding "jal" instruction
  //   ImmType = 00 -> lui, jal and j
  //   ImmType = 01 -> b
  //   ImmType = 10 -> logical-arithmetical instructions
  //   if it is an arithmetical operation (a) this is used to put 
  //   ALUOut = shifter ouput insted of arithmetical output
  //   left shift if 0, right shift if 1
  //   It's active only with a "store" instruction
  //   MemToReg = MemRead = a and not b and not c and d and not e
  //   It's active only with a "load" instruction"
endmodule
