// Logisim project data_memory.circ as structural Verilog: 3 circuits, main circuit data_memory
module data_memory (
  input  Size,
  input  MemWrite,
  input  CLK,
  input  MemRead,
  input  [15:0] WriteData,
  input  [15:0] Address,
  output [15:0] ReadData
);

  wire and_1_out, and_2_out, n74283_1_pin2, n74283_1_pin7, n74283_2_pin7, n74283_3_pin7, n74283_4_pin7,
       nand_1_out, not_1_out, or_1_out;
  wire [0:0] multiplexer_1_out, multiplexer_2_out;
  wire [14:0] multiplexer_1_out_2, multiplexer_2_out_2;
  wire [15:0] n74283_4_pin4;

  _74283 u_74283_1 (
    .pin1(n74283_4_pin4[13]), .pin2(n74283_1_pin2), .pin3(Address[13]), .pin4(n74283_4_pin4[12]),
    .pin5(Address[12]), .pin6(n74283_1_pin2), .pin7(n74283_1_pin7), .pin15(n74283_1_pin2),
    .pin14(Address[14]), .pin13(n74283_4_pin4[14]), .pin12(Address[15]), .pin11(n74283_1_pin2),
    .pin10(n74283_4_pin4[15]));  // open: pin9
  _74283 u_74283_2 (
    .pin1(n74283_4_pin4[9]), .pin2(n74283_1_pin2), .pin3(Address[9]), .pin4(n74283_4_pin4[8]),
    .pin5(Address[8]), .pin6(n74283_1_pin2), .pin7(n74283_2_pin7), .pin15(n74283_1_pin2),
    .pin14(Address[10]), .pin13(n74283_4_pin4[10]), .pin12(Address[11]), .pin11(n74283_1_pin2),
    .pin10(n74283_4_pin4[11]), .pin9(n74283_1_pin7));
  _74283 u_74283_3 (
    .pin1(n74283_4_pin4[5]), .pin2(n74283_1_pin2), .pin3(Address[5]), .pin4(n74283_4_pin4[4]),
    .pin5(Address[4]), .pin6(n74283_1_pin2), .pin7(n74283_3_pin7), .pin15(n74283_1_pin2), .pin14(Address[6]),
    .pin13(n74283_4_pin4[6]), .pin12(Address[7]), .pin11(n74283_1_pin2), .pin10(n74283_4_pin4[7]),
    .pin9(n74283_2_pin7));
  Multiplexer #(.width(16)) multiplexer_1 (
    .in0(Address), .in1(n74283_4_pin4), .out({multiplexer_1_out_2, multiplexer_1_out[0]}), .sel(Address[0]));
  Multiplexer #(.width(16)) multiplexer_2 (
    .in0(n74283_4_pin4), .in1(Address), .out({multiplexer_2_out_2, multiplexer_2_out[0]}), .sel(Address[0]));
  _74283 u_74283_4 (
    .pin1(n74283_4_pin4[1]), .pin2(n74283_1_pin2), .pin3(Address[1]), .pin4(n74283_4_pin4[0]),
    .pin5(Address[0]), .pin6(n74283_1_pin2), .pin7(n74283_4_pin7), .pin15(n74283_1_pin2), .pin14(Address[2]),
    .pin13(n74283_4_pin4[2]), .pin12(Address[3]), .pin11(n74283_1_pin2), .pin10(n74283_4_pin4[3]),
    .pin9(n74283_3_pin7));
  not not_1 (not_1_out, Size);
  nand nand_1 (nand_1_out, not_1_out, Address[0]);
  or or_1 (or_1_out, Size, Address[0]);
  RAM #(.addrWidth(16)) ram_1 (
    .addr({1'b0, multiplexer_1_out_2}), .we(and_1_out), .oe(MemRead), .clk(CLK), .din(WriteData[7:0]),
    .dout(ReadData[7:0]));
  and and_1 (and_1_out, MemWrite, nand_1_out);
  RAM #(.addrWidth(16)) ram_2 (
    .addr({1'b0, multiplexer_2_out_2}), .we(and_2_out), .oe(MemRead), .clk(CLK), .din(WriteData[15:8]),
    .dout(ReadData[15:8]));
  and and_2 (and_2_out, MemWrite, or_1_out);
  // also tied to GND on the sheet: n74283_1_pin2
  // also tied to VCC on the sheet: n74283_4_pin7

  // Notes on the sheet:
  //   Size: 0 if 8 bit, 1 if 16
  //   this is a right shift of 1 bit
  //   this is a right shift of 1 bit
endmodule

module trash (
  input  CLK,
  input  Size,
  input  WE,
  input  [15:0] WriteData,
  input  [15:0] Address,
  output [15:0] ReadData
);

  wire and_1_out, and_2_out, and_3_out, and_4_out, and_5_out, n74273_1_pin11, n74273_3_pin1, n74283_1_pin2,
       n74283_1_pin7, n74283_2_pin7, n74283_3_pin7, n74283_4_pin7, or_1_out, undriven;
  wire [7:0] demultiplexer_1_out0, demultiplexer_1_out1, multiplexer_1_out, n74273_1_pin2, n74273_1_pin3,
       n74273_2_pin2, n74273_2_pin3, ram_1_dout;
  wire [15:0] n74283_4_pin4;

  _74273 u_74273_1 (
    .pin2(n74273_1_pin2[0]), .pin3(n74273_1_pin3[0]), .pin4(n74273_1_pin3[1]), .pin5(n74273_1_pin2[1]),
    .pin6(n74273_1_pin2[2]), .pin7(n74273_1_pin3[2]), .pin8(n74273_1_pin3[3]), .pin9(n74273_1_pin2[3]),
    .pin19(n74273_1_pin2[7]), .pin18(n74273_1_pin3[7]), .pin17(n74273_1_pin3[6]), .pin16(n74273_1_pin2[6]),
    .pin15(n74273_1_pin2[5]), .pin14(n74273_1_pin3[5]), .pin13(n74273_1_pin3[4]), .pin12(n74273_1_pin2[4]),
    .pin11(n74273_1_pin11));  // open: pin1
  _74273 u_74273_2 (
    .pin2(n74273_2_pin2[0]), .pin3(n74273_2_pin3[0]), .pin4(n74273_2_pin3[1]), .pin5(n74273_2_pin2[1]),
    .pin6(n74273_2_pin2[2]), .pin7(n74273_2_pin3[2]), .pin8(n74273_2_pin3[3]), .pin9(n74273_2_pin2[3]),
    .pin19(n74273_2_pin2[7]), .pin18(n74273_2_pin3[7]), .pin17(n74273_2_pin3[6]), .pin16(n74273_2_pin2[6]),
    .pin15(n74273_2_pin2[5]), .pin14(n74273_2_pin3[5]), .pin13(n74273_2_pin3[4]), .pin12(n74273_2_pin2[4]),
    .pin11(n74273_1_pin11));  // open: pin1
  Multiplexer #(.width(8)) multiplexer_1 (
    .in0(WriteData[15:8]), .in1(WriteData[7:0]), .out(multiplexer_1_out), .sel(undriven));
  _74283 u_74283_1 (
    .pin1(n74283_4_pin4[13]), .pin2(n74283_1_pin2), .pin3(Address[13]), .pin4(n74283_4_pin4[12]),
    .pin5(Address[12]), .pin6(n74283_1_pin2), .pin7(n74283_1_pin7), .pin15(n74283_1_pin2),
    .pin14(Address[14]), .pin13(n74283_4_pin4[14]), .pin12(Address[15]), .pin11(n74283_1_pin2),
    .pin10(n74283_4_pin4[15]));  // open: pin9
  and and_1 (and_1_out, CLK, CLK);
  and and_2 (and_2_out, and_1_out, and_1_out);
  and and_3 (and_3_out, and_2_out, and_2_out);
  and and_4 (and_4_out, and_3_out, and_3_out);
  _74283 u_74283_2 (
    .pin1(n74283_4_pin4[9]), .pin2(n74283_1_pin2), .pin3(Address[9]), .pin4(n74283_4_pin4[8]),
    .pin5(Address[8]), .pin6(n74283_1_pin2), .pin7(n74283_2_pin7), .pin15(n74283_1_pin2),
    .pin14(Address[10]), .pin13(n74283_4_pin4[10]), .pin12(Address[11]), .pin11(n74283_1_pin2),
    .pin10(n74283_4_pin4[11]), .pin9(n74283_1_pin7));
  or or_1 (or_1_out, CLK, Size);
  and and_5 (and_5_out, or_1_out, WE);
  RAM #(.addrWidth(16)) ram_1 (
    .addr(n74283_4_pin4), .we(and_5_out), .oe(1'b1), .clk(and_4_out), .din(multiplexer_1_out),
    .dout(ram_1_dout));
  _74283 u_74283_3 (
    .pin1(n74283_4_pin4[5]), .pin2(n74283_1_pin2), .pin3(Address[5]), .pin4(n74283_4_pin4[4]),
    .pin5(Address[4]), .pin6(n74283_1_pin2), .pin7(n74283_3_pin7), .pin15(n74283_1_pin2), .pin14(Address[6]),
    .pin13(n74283_4_pin4[6]), .pin12(Address[7]), .pin11(n74283_1_pin2), .pin10(n74283_4_pin4[7]),
    .pin9(n74283_2_pin7));
  _74283 u_74283_4 (
    .pin1(n74283_4_pin4[1]), .pin2(n74283_1_pin2), .pin3(Address[1]), .pin4(n74283_4_pin4[0]),
    .pin5(Address[0]), .pin6(n74283_1_pin2), .pin7(n74283_4_pin7), .pin15(n74283_1_pin2), .pin14(Address[2]),
    .pin13(n74283_4_pin4[2]), .pin12(Address[3]), .pin11(n74283_1_pin2), .pin10(n74283_4_pin4[3]),
    .pin9(n74283_3_pin7));
  Demultiplexer #(.width(8)) demultiplexer_1 (
    .out0(demultiplexer_1_out0), .out1(demultiplexer_1_out1), .in(ram_1_dout), .sel(undriven));
  not not_1 (n74283_4_pin7, CLK);
  _74273 u_74273_3 (
    .pin1(n74273_3_pin1), .pin2(ReadData[8]), .pin3(demultiplexer_1_out0[0]), .pin4(demultiplexer_1_out0[1]),
    .pin5(ReadData[9]), .pin6(ReadData[10]), .pin7(demultiplexer_1_out0[2]), .pin8(demultiplexer_1_out0[3]),
    .pin9(ReadData[11]), .pin19(ReadData[15]), .pin18(demultiplexer_1_out0[7]),
    .pin17(demultiplexer_1_out0[6]), .pin16(ReadData[14]), .pin15(ReadData[13]),
    .pin14(demultiplexer_1_out0[5]), .pin13(demultiplexer_1_out0[4]), .pin12(ReadData[12]));  // open: pin11
  _74273 u_74273_4 (
    .pin2(ReadData[0]), .pin3(demultiplexer_1_out1[0]), .pin4(demultiplexer_1_out1[1]), .pin5(ReadData[1]),
    .pin6(ReadData[2]), .pin7(demultiplexer_1_out1[2]), .pin8(demultiplexer_1_out1[3]), .pin9(ReadData[3]),
    .pin19(ReadData[7]), .pin18(demultiplexer_1_out1[7]), .pin17(demultiplexer_1_out1[6]),
    .pin16(ReadData[6]), .pin15(ReadData[5]), .pin14(demultiplexer_1_out1[5]),
    .pin13(demultiplexer_1_out1[4]), .pin12(ReadData[4]));  // open: pin1, pin11
  not not_2 (n74273_3_pin1, Size);
  // also tied to GND on the sheet: n74283_1_pin2

  // Notes on the sheet:
  //   NOT WORKING, MAYBE I SHOULD USE 2 MEMORY IN PARALLEL
  //   WHEN I WILL HAVE TO TEST THIS WITH VHDL, I SHOULD USE ALDEC VHDL SOFTWARE
  //   I HAVE TO ADD A CONDITION TO WRITE TO THE REGISTER
  //   I WRITE TO IT ONLY IF REGISTER IS SELECTED
  //   HIGHER BYTE (8-15)
  //   LOWER BYTE (0-7)
  //   since it's little endiand, first is written lower byte
  //   this brought me to map lower byte to "1" mux port
  //   so when clock is high, the first byte is selected
  //   When clock turns low, the second byte is selected
endmodule

module data_memory_separate_inputs (
  input  Size,
  input  MemWrite,
  input  CLK,
  input  MemRead,
  input  [7:0] WriteData0,
  input  [7:0] WriteData1,
  input  [15:0] Address,
  output [15:0] ReadData
);

  wire and_1_out, and_2_out, n74283_1_pin2, n74283_1_pin7, n74283_2_pin7, n74283_3_pin7, n74283_4_pin7,
       nand_1_out, not_1_out, or_1_out;
  wire [0:0] multiplexer_1_out, multiplexer_2_out;
  wire [14:0] multiplexer_1_out_2, multiplexer_2_out_2;
  wire [15:0] n74283_4_pin4;

  _74283 u_74283_1 (
    .pin1(n74283_4_pin4[13]), .pin2(n74283_1_pin2), .pin3(Address[13]), .pin4(n74283_4_pin4[12]),
    .pin5(Address[12]), .pin6(n74283_1_pin2), .pin7(n74283_1_pin7), .pin15(n74283_1_pin2),
    .pin14(Address[14]), .pin13(n74283_4_pin4[14]), .pin12(Address[15]), .pin11(n74283_1_pin2),
    .pin10(n74283_4_pin4[15]));  // open: pin9
  _74283 u_74283_2 (
    .pin1(n74283_4_pin4[9]), .pin2(n74283_1_pin2), .pin3(Address[9]), .pin4(n74283_4_pin4[8]),
    .pin5(Address[8]), .pin6(n74283_1_pin2), .pin7(n74283_2_pin7), .pin15(n74283_1_pin2),
    .pin14(Address[10]), .pin13(n74283_4_pin4[10]), .pin12(Address[11]), .pin11(n74283_1_pin2),
    .pin10(n74283_4_pin4[11]), .pin9(n74283_1_pin7));
  _74283 u_74283_3 (
    .pin1(n74283_4_pin4[5]), .pin2(n74283_1_pin2), .pin3(Address[5]), .pin4(n74283_4_pin4[4]),
    .pin5(Address[4]), .pin6(n74283_1_pin2), .pin7(n74283_3_pin7), .pin15(n74283_1_pin2), .pin14(Address[6]),
    .pin13(n74283_4_pin4[6]), .pin12(Address[7]), .pin11(n74283_1_pin2), .pin10(n74283_4_pin4[7]),
    .pin9(n74283_2_pin7));
  Multiplexer #(.width(16)) multiplexer_1 (
    .in0(Address), .in1(n74283_4_pin4), .out({multiplexer_1_out_2, multiplexer_1_out[0]}), .sel(Address[0]));
  Multiplexer #(.width(16)) multiplexer_2 (
    .in0(n74283_4_pin4), .in1(Address), .out({multiplexer_2_out_2, multiplexer_2_out[0]}), .sel(Address[0]));
  _74283 u_74283_4 (
    .pin1(n74283_4_pin4[1]), .pin2(n74283_1_pin2), .pin3(Address[1]), .pin4(n74283_4_pin4[0]),
    .pin5(Address[0]), .pin6(n74283_1_pin2), .pin7(n74283_4_pin7), .pin15(n74283_1_pin2), .pin14(Address[2]),
    .pin13(n74283_4_pin4[2]), .pin12(Address[3]), .pin11(n74283_1_pin2), .pin10(n74283_4_pin4[3]),
    .pin9(n74283_3_pin7));
  not not_1 (not_1_out, Size);
  nand nand_1 (nand_1_out, not_1_out, Address[0]);
  or or_1 (or_1_out, Size, Address[0]);
  RAM #(.addrWidth(16)) ram_1 (
    .addr({1'b0, multiplexer_1_out_2}), .we(and_1_out), .oe(MemRead), .clk(CLK), .din(WriteData0),
    .dout(ReadData[7:0]));
  and and_1 (and_1_out, MemWrite, nand_1_out);
  RAM #(.addrWidth(16)) ram_2 (
    .addr({1'b0, multiplexer_2_out_2}), .we(and_2_out), .oe(MemRead), .clk(CLK), .din(WriteData1),
    .dout(ReadData[15:8]));
  and and_2 (and_2_out, MemWrite, or_1_out);
  // also tied to GND on the sheet: n74283_1_pin2
  // also tied to VCC on the sheet: n74283_4_pin7

  // Notes on the sheet:
  //   Lower Byte
  //   Higher Byte
  //   Size: 0 if 8 bit, 1 if 16
  //   this is a right shift of 1 bit
  //   this is a right shift of 1 bit
endmodule
