// Logisim project delayer.circ as structural Verilog: 5 circuits, main circuit delayer_10AND
module delayer_10AND (
  input  Inp,
  output Outp
);

  wire delayer_5and_1_outp;

  delayer_5AND delayer_5and_1 (.Inp(Inp), .Outp(delayer_5and_1_outp));
  delayer_5AND delayer_5and_2 (.Inp(delayer_5and_1_outp), .Outp(Outp));
endmodule

module delayer_sigext_60AND (
  input  Inp,
  output Outp
);

  wire clock_1_out, delayer_20and_2_outp, delayer_20and_3_outp, delayer_40and_1_outp, delayer_40and_2_outp;

  Clock clock_1 (.out(clock_1_out));
  delayer_40AND delayer_40and_1 (.Inp(clock_1_out), .Outp(delayer_40and_1_outp));
  delayer_40AND delayer_40and_2 (.Inp(clock_1_out), .Outp(delayer_40and_2_outp));
  delayer_20AND delayer_20and_1 (.Inp(delayer_40and_2_outp));  // open: Outp
  delayer_20AND delayer_20and_2 (.Inp(delayer_40and_1_outp), .Outp(delayer_20and_2_outp));
  delayer_20AND delayer_20and_3 (.Outp(delayer_20and_3_outp));  // open: Inp
  or or_1 (Outp, delayer_20and_2_outp, delayer_20and_3_outp);
endmodule

module delayer_5AND (
  input  Inp,
  output Outp
);

  wire and_1_out, and_2_out, and_3_out, and_4_out;

  and and_1 (and_1_out, Inp, Inp);
  and and_2 (and_2_out, and_1_out, and_1_out);
  and and_3 (and_3_out, and_2_out, and_2_out);
  and and_4 (and_4_out, and_3_out, and_3_out);
  and and_5 (Outp, and_4_out, and_4_out);
endmodule

module delayer_20AND (
  input  Inp,
  output Outp
);

  wire delayer_10and_1_outp;

  delayer_10AND delayer_10and_1 (.Inp(Inp), .Outp(delayer_10and_1_outp));
  delayer_10AND delayer_10and_2 (.Inp(delayer_10and_1_outp), .Outp(Outp));
endmodule

module delayer_40AND (
  input  Inp,
  output Outp
);

  wire delayer_20and_1_outp;

  delayer_20AND delayer_20and_1 (.Inp(Inp), .Outp(delayer_20and_1_outp));
  delayer_20AND delayer_20and_2 (.Inp(delayer_20and_1_outp), .Outp(Outp));
endmodule
