// Logisim project instruction_decoder.circ as structural Verilog: 1 circuit, main circuit instruction_decoder
module instruction_decoder (
  input  [15:0] Instruction,
  output [4:0] OpCode,
  output [2:0] Mask,
  output [3:0] rd,
  output [3:0] rs,
  output Type_Size,
  output [9:0] Immediate
);


  assign Immediate = Instruction[14:5];
  assign Mask = {Instruction[15], Instruction[6:5]};
  assign OpCode = Instruction[4:0];
  assign rd = Instruction[8:5];
  assign rs = Instruction[12:9];
  assign Type_Size = Instruction[15];
endmodule
