// Logisim project register_file.circ as structural Verilog: 1 circuit, main circuit register_file
module register_file (
  input  CLK,
  input  RegWrite,
  input  Size,
  input  [3:0] WriteAddr,
  input  [15:0] WriteData,
  input  [3:0] ReadAddr0,
  input  [3:0] ReadAddr1,
  output [15:0] ReadData0,
  output [15:0] ReadData1
);

  wire and_1_out, and_2_out, and_3_out, and_4_out, and_5_out, and_6_out, and_7_out, and_8_out, and_9_out,
       decoder_1_out0, decoder_1_out1, decoder_1_out2, decoder_1_out3, decoder_1_out4, decoder_1_out5,
       decoder_1_out6, decoder_1_out7, not_1_out;
  wire [15:0] n74273_1_pin2, n74273_3_pin2, n74273_5_pin2, n74273_7_pin2, n74273_9_pin2, n74273_11_pin2,
       n74273_13_pin2, n74273_15_pin2;

  and and_1 (and_1_out, CLK, RegWrite);
  not not_1 (not_1_out, Size);
  Decoder #(.enable("false"), .select(4)) decoder_1 (
    .out0(decoder_1_out0), .out1(decoder_1_out1), .out2(decoder_1_out2), .out3(decoder_1_out3),
    .out4(decoder_1_out4), .out5(decoder_1_out5), .out6(decoder_1_out6), .out7(decoder_1_out7),
    .sel(WriteAddr));  // open: out8, out9, out10, out11, out12, out13, out14, out15
  and and_2 (and_2_out, decoder_1_out3, and_1_out);
  and and_3 (and_3_out, decoder_1_out7, and_1_out);
  _74273 u_74273_1 (
    .pin2(n74273_1_pin2[0]), .pin3(WriteData[0]), .pin4(WriteData[1]), .pin5(n74273_1_pin2[1]),
    .pin6(n74273_1_pin2[2]), .pin7(WriteData[2]), .pin8(WriteData[3]), .pin9(n74273_1_pin2[3]),
    .pin19(n74273_1_pin2[7]), .pin18(WriteData[7]), .pin17(WriteData[6]), .pin16(n74273_1_pin2[6]),
    .pin15(n74273_1_pin2[5]), .pin14(WriteData[5]), .pin13(WriteData[4]), .pin12(n74273_1_pin2[4]),
    .pin11(and_2_out));  // open: pin1
  _74273 u_74273_2 (
    .pin1(not_1_out), .pin2(n74273_1_pin2[8]), .pin3(WriteData[8]), .pin4(WriteData[9]),
    .pin5(n74273_1_pin2[9]), .pin6(n74273_1_pin2[10]), .pin7(WriteData[10]), .pin8(WriteData[11]),
    .pin9(n74273_1_pin2[11]), .pin19(n74273_1_pin2[15]), .pin18(WriteData[15]), .pin17(WriteData[14]),
    .pin16(n74273_1_pin2[14]), .pin15(n74273_1_pin2[13]), .pin14(WriteData[13]), .pin13(WriteData[12]),
    .pin12(n74273_1_pin2[12]), .pin11(and_2_out));
  _74273 u_74273_3 (
    .pin2(n74273_3_pin2[0]), .pin3(WriteData[0]), .pin4(WriteData[1]), .pin5(n74273_3_pin2[1]),
    .pin6(n74273_3_pin2[2]), .pin7(WriteData[2]), .pin8(WriteData[3]), .pin9(n74273_3_pin2[3]),
    .pin19(n74273_3_pin2[7]), .pin18(WriteData[7]), .pin17(WriteData[6]), .pin16(n74273_3_pin2[6]),
    .pin15(n74273_3_pin2[5]), .pin14(WriteData[5]), .pin13(WriteData[4]), .pin12(n74273_3_pin2[4]),
    .pin11(and_3_out));  // open: pin1
  _74273 u_74273_4 (
    .pin1(not_1_out), .pin2(n74273_3_pin2[8]), .pin3(WriteData[8]), .pin4(WriteData[9]),
    .pin5(n74273_3_pin2[9]), .pin6(n74273_3_pin2[10]), .pin7(WriteData[10]), .pin8(WriteData[11]),
    .pin9(n74273_3_pin2[11]), .pin19(n74273_3_pin2[15]), .pin18(WriteData[15]), .pin17(WriteData[14]),
    .pin16(n74273_3_pin2[14]), .pin15(n74273_3_pin2[13]), .pin14(WriteData[13]), .pin13(WriteData[12]),
    .pin12(n74273_3_pin2[12]), .pin11(and_3_out));
  and and_4 (and_4_out, decoder_1_out2, and_1_out);
  and and_5 (and_5_out, decoder_1_out6, and_1_out);
  _74273 u_74273_5 (
    .pin2(n74273_5_pin2[0]), .pin3(WriteData[0]), .pin4(WriteData[1]), .pin5(n74273_5_pin2[1]),
    .pin6(n74273_5_pin2[2]), .pin7(WriteData[2]), .pin8(WriteData[3]), .pin9(n74273_5_pin2[3]),
    .pin19(n74273_5_pin2[7]), .pin18(WriteData[7]), .pin17(WriteData[6]), .pin16(n74273_5_pin2[6]),
    .pin15(n74273_5_pin2[5]), .pin14(WriteData[5]), .pin13(WriteData[4]), .pin12(n74273_5_pin2[4]),
    .pin11(and_4_out));  // open: pin1
  _74273 u_74273_6 (
    .pin1(not_1_out), .pin2(n74273_5_pin2[8]), .pin3(WriteData[8]), .pin4(WriteData[9]),
    .pin5(n74273_5_pin2[9]), .pin6(n74273_5_pin2[10]), .pin7(WriteData[10]), .pin8(WriteData[11]),
    .pin9(n74273_5_pin2[11]), .pin19(n74273_5_pin2[15]), .pin18(WriteData[15]), .pin17(WriteData[14]),
    .pin16(n74273_5_pin2[14]), .pin15(n74273_5_pin2[13]), .pin14(WriteData[13]), .pin13(WriteData[12]),
    .pin12(n74273_5_pin2[12]), .pin11(and_4_out));
  _74273 u_74273_7 (
    .pin2(n74273_7_pin2[0]), .pin3(WriteData[0]), .pin4(WriteData[1]), .pin5(n74273_7_pin2[1]),
    .pin6(n74273_7_pin2[2]), .pin7(WriteData[2]), .pin8(WriteData[3]), .pin9(n74273_7_pin2[3]),
    .pin19(n74273_7_pin2[7]), .pin18(WriteData[7]), .pin17(WriteData[6]), .pin16(n74273_7_pin2[6]),
    .pin15(n74273_7_pin2[5]), .pin14(WriteData[5]), .pin13(WriteData[4]), .pin12(n74273_7_pin2[4]),
    .pin11(and_5_out));  // open: pin1
  _74273 u_74273_8 (
    .pin1(not_1_out), .pin2(n74273_7_pin2[8]), .pin3(WriteData[8]), .pin4(WriteData[9]),
    .pin5(n74273_7_pin2[9]), .pin6(n74273_7_pin2[10]), .pin7(WriteData[10]), .pin8(WriteData[11]),
    .pin9(n74273_7_pin2[11]), .pin19(n74273_7_pin2[15]), .pin18(WriteData[15]), .pin17(WriteData[14]),
    .pin16(n74273_7_pin2[14]), .pin15(n74273_7_pin2[13]), .pin14(WriteData[13]), .pin13(WriteData[12]),
    .pin12(n74273_7_pin2[12]), .pin11(and_5_out));
  and and_6 (and_6_out, decoder_1_out1, and_1_out);
  and and_7 (and_7_out, decoder_1_out5, and_1_out);
  _74273 u_74273_9 (
    .pin2(n74273_9_pin2[0]), .pin3(WriteData[0]), .pin4(WriteData[1]), .pin5(n74273_9_pin2[1]),
    .pin6(n74273_9_pin2[2]), .pin7(WriteData[2]), .pin8(WriteData[3]), .pin9(n74273_9_pin2[3]),
    .pin19(n74273_9_pin2[7]), .pin18(WriteData[7]), .pin17(WriteData[6]), .pin16(n74273_9_pin2[6]),
    .pin15(n74273_9_pin2[5]), .pin14(WriteData[5]), .pin13(WriteData[4]), .pin12(n74273_9_pin2[4]),
    .pin11(and_6_out));  // open: pin1
  _74273 u_74273_10 (
    .pin1(not_1_out), .pin2(n74273_9_pin2[8]), .pin3(WriteData[8]), .pin4(WriteData[9]),
    .pin5(n74273_9_pin2[9]), .pin6(n74273_9_pin2[10]), .pin7(WriteData[10]), .pin8(WriteData[11]),
    .pin9(n74273_9_pin2[11]), .pin19(n74273_9_pin2[15]), .pin18(WriteData[15]), .pin17(WriteData[14]),
    .pin16(n74273_9_pin2[14]), .pin15(n74273_9_pin2[13]), .pin14(WriteData[13]), .pin13(WriteData[12]),
    .pin12(n74273_9_pin2[12]), .pin11(and_6_out));
  _74273 u_74273_11 (
    .pin2(n74273_11_pin2[0]), .pin3(WriteData[0]), .pin4(WriteData[1]), .pin5(n74273_11_pin2[1]),
    .pin6(n74273_11_pin2[2]), .pin7(WriteData[2]), .pin8(WriteData[3]), .pin9(n74273_11_pin2[3]),
    .pin19(n74273_11_pin2[7]), .pin18(WriteData[7]), .pin17(WriteData[6]), .pin16(n74273_11_pin2[6]),
    .pin15(n74273_11_pin2[5]), .pin14(WriteData[5]), .pin13(WriteData[4]), .pin12(n74273_11_pin2[4]),
    .pin11(and_7_out));  // open: pin1
  _74273 u_74273_12 (
    .pin1(not_1_out), .pin2(n74273_11_pin2[8]), .pin3(WriteData[8]), .pin4(WriteData[9]),
    .pin5(n74273_11_pin2[9]), .pin6(n74273_11_pin2[10]), .pin7(WriteData[10]), .pin8(WriteData[11]),
    .pin9(n74273_11_pin2[11]), .pin19(n74273_11_pin2[15]), .pin18(WriteData[15]), .pin17(WriteData[14]),
    .pin16(n74273_11_pin2[14]), .pin15(n74273_11_pin2[13]), .pin14(WriteData[13]), .pin13(WriteData[12]),
    .pin12(n74273_11_pin2[12]), .pin11(and_7_out));
  and and_8 (and_8_out, decoder_1_out0, and_1_out);
  _74273 u_74273_13 (
    .pin2(n74273_13_pin2[0]), .pin3(WriteData[0]), .pin4(WriteData[1]), .pin5(n74273_13_pin2[1]),
    .pin6(n74273_13_pin2[2]), .pin7(WriteData[2]), .pin8(WriteData[3]), .pin9(n74273_13_pin2[3]),
    .pin19(n74273_13_pin2[7]), .pin18(WriteData[7]), .pin17(WriteData[6]), .pin16(n74273_13_pin2[6]),
    .pin15(n74273_13_pin2[5]), .pin14(WriteData[5]), .pin13(WriteData[4]), .pin12(n74273_13_pin2[4]),
    .pin11(and_8_out));  // open: pin1
  _74273 u_74273_14 (
    .pin1(not_1_out), .pin2(n74273_13_pin2[8]), .pin3(WriteData[8]), .pin4(WriteData[9]),
    .pin5(n74273_13_pin2[9]), .pin6(n74273_13_pin2[10]), .pin7(WriteData[10]), .pin8(WriteData[11]),
    .pin9(n74273_13_pin2[11]), .pin19(n74273_13_pin2[15]), .pin18(WriteData[15]), .pin17(WriteData[14]),
    .pin16(n74273_13_pin2[14]), .pin15(n74273_13_pin2[13]), .pin14(WriteData[13]), .pin13(WriteData[12]),
    .pin12(n74273_13_pin2[12]), .pin11(and_8_out));
  and and_9 (and_9_out, decoder_1_out4, and_1_out);
  _74273 u_74273_15 (
    .pin2(n74273_15_pin2[0]), .pin3(WriteData[0]), .pin4(WriteData[1]), .pin5(n74273_15_pin2[1]),
    .pin6(n74273_15_pin2[2]), .pin7(WriteData[2]), .pin8(WriteData[3]), .pin9(n74273_15_pin2[3]),
    .pin19(n74273_15_pin2[7]), .pin18(WriteData[7]), .pin17(WriteData[6]), .pin16(n74273_15_pin2[6]),
    .pin15(n74273_15_pin2[5]), .pin14(WriteData[5]), .pin13(WriteData[4]), .pin12(n74273_15_pin2[4]),
    .pin11(and_9_out));  // open: pin1
  _74273 u_74273_16 (
    .pin1(not_1_out), .pin2(n74273_15_pin2[8]), .pin3(WriteData[8]), .pin4(WriteData[9]),
    .pin5(n74273_15_pin2[9]), .pin6(n74273_15_pin2[10]), .pin7(WriteData[10]), .pin8(WriteData[11]),
    .pin9(n74273_15_pin2[11]), .pin19(n74273_15_pin2[15]), .pin18(WriteData[15]), .pin17(WriteData[14]),
    .pin16(n74273_15_pin2[14]), .pin15(n74273_15_pin2[13]), .pin14(WriteData[13]), .pin13(WriteData[12]),
    .pin12(n74273_15_pin2[12]), .pin11(and_9_out));
  Multiplexer #(.select(4), .width(16)) multiplexer_1 (
    .in0(n74273_13_pin2), .in1(n74273_9_pin2), .in2(n74273_5_pin2), .in3(n74273_1_pin2),
    .in4(n74273_15_pin2), .in5(n74273_11_pin2), .in6(n74273_7_pin2), .in7(n74273_3_pin2), .out(ReadData0),
    .sel(ReadAddr0));  // open: in8, in9, in10, in11, in12, in13, in14, in15
  Multiplexer #(.select(4), .width(16)) multiplexer_2 (
    .in0(n74273_13_pin2), .in1(n74273_9_pin2), .in2(n74273_5_pin2), .in3(n74273_1_pin2),
    .in4(n74273_15_pin2), .in5(n74273_11_pin2), .in6(n74273_7_pin2), .in7(n74273_3_pin2), .out(ReadData1),
    .sel(ReadAddr1));  // open: in8, in9, in10, in11, in12, in13, in14, in15

  // Notes on the sheet:
  //   0 if 8 bit, 1 if 16 bit
  //   t3 -> 0011
  //   sp -> 0111
  //   t2 -> 0010
  //   a2 -> 0110
  //   t1 -> 0001
  //   a1 -> 0101
  //   t0 -> 0000
  //   a0 -> 0100
endmodule
